# Fritzing sketch Teehalter_projekt (saved by Fritzing 0.9.4)
breadboards: 1

parts:
  U1 = NodeMCU V1.0
  J1 = Basic Servo
  Grove1 = Grove OLED 128x96
  S1 = Momentary Switch [package=ksa_sealed_tac_switch]
  R1 = Resistor [tolerance=±5% resistance=330 package="0402 [SMD]"]
  S2 = Momentary Switch [package=ksa_sealed_tac_switch]
  R2 = Resistor [tolerance=±5% resistance=330 package="0402 [SMD]"]
  J2 = Piezo Speaker

nets:
  N1: U1.D1, Grove1.SCL
  N2: U1.D2, Grove1.SDA
  3V3: U1.3V3, Grove1.VCC
  GND: U1.GND, J1.gnd, Grove1.GND, S1.2, R1.Pin_1, S2.2, R2.Pin_1, J2.pin1
  N3: U1.D5, S1.1, R1.Pin_0
  N4: U1.D6, S2.1, R2.Pin_0
  N5: U1.D7, J1.pulse
  N6: U1.D8, J2.pin2
  VIN: U1.Vin, J1.vcc, S1.3, S1.4, S2.3, S2.4

custom parts:
  NodeMCU V1.0: ESP8266 based NodeMCU
